// Logisim project 10bit alu.circ as structural Verilog: 1 circuit, main circuit main
module main (
  input  B_prime,
  input  Cin,
  input  [9:0] A,
  input  [9:0] B,
  input  [2:0] Op,
  output [9:0] Result,
  output Cout
);

  wire main_1_c_out, main_2_c_out, main_3_c_out, main_4_c_out, main_5_c_out, main_6_c_out, main_7_c_out,
       main_8_c_out, main_9_c_out;

  _1bit_alu_main main_1 (
    .Cin(Cin), .B_prime(B_prime), .op(Op), .result(Result[0]), .C_out(main_1_c_out), .B0(B[0]), .A0(A[0]));
  _1bit_alu_main main_2 (
    .Cin(main_1_c_out), .B_prime(B_prime), .op(Op), .result(Result[1]), .C_out(main_2_c_out), .B0(B[1]),
    .A0(A[1]));
  _1bit_alu_main main_3 (
    .Cin(main_2_c_out), .B_prime(B_prime), .op(Op), .result(Result[2]), .C_out(main_3_c_out), .B0(B[2]),
    .A0(A[2]));
  _1bit_alu_main main_4 (
    .Cin(main_3_c_out), .B_prime(B_prime), .op(Op), .result(Result[3]), .C_out(main_4_c_out), .B0(B[3]),
    .A0(A[3]));
  _1bit_alu_main main_5 (
    .Cin(main_4_c_out), .B_prime(B_prime), .op(Op), .result(Result[4]), .C_out(main_5_c_out), .B0(B[4]),
    .A0(A[4]));
  _1bit_alu_main main_6 (
    .Cin(main_5_c_out), .B_prime(B_prime), .op(Op), .result(Result[5]), .C_out(main_6_c_out), .B0(B[5]),
    .A0(A[5]));
  _1bit_alu_main main_7 (
    .Cin(main_6_c_out), .B_prime(B_prime), .op(Op), .result(Result[6]), .C_out(main_7_c_out), .B0(B[6]),
    .A0(A[6]));
  _1bit_alu_main main_8 (
    .Cin(main_7_c_out), .B_prime(B_prime), .op(Op), .result(Result[7]), .C_out(main_8_c_out), .B0(B[7]),
    .A0(A[7]));
  _1bit_alu_main main_9 (
    .Cin(main_8_c_out), .B_prime(B_prime), .op(Op), .result(Result[8]), .C_out(main_9_c_out), .B0(B[8]),
    .A0(A[8]));
  _1bit_alu_main main_10 (
    .Cin(main_9_c_out), .B_prime(B_prime), .op(Op), .result(Result[9]), .C_out(Cout), .B0(B[9]), .A0(A[9]));
endmodule
