// Logisim project 1bit alu.circ as structural Verilog: 1 circuit, main circuit main
module main (
  input  Cin,
  input  B0,
  input  A0,
  input  B_prime,
  input  [2:0] op,
  output result,
  output C_out
);

  wire adder_1_out, and_1_out, multiplexer_1_out, nor_1_out, not_1_out, or_1_out, xor_1_out;

  not not_1 (not_1_out, B0);
  Multiplexer multiplexer_1 (.in0(B0), .in1(not_1_out), .out(multiplexer_1_out), .sel(B_prime));  // open: en
  and and_1 (and_1_out, A0, B0);
  or or_1 (or_1_out, A0, B0);
  nor nor_1 (nor_1_out, A0, B0);
  xor xor_1 (xor_1_out, A0, B0);
  Adder #(.width(1)) adder_1 (.a(A0), .b(multiplexer_1_out), .out(adder_1_out), .cin(Cin), .cout(C_out));
  Multiplexer #(.select(3)) multiplexer_2 (
    .in0(adder_1_out), .in1(and_1_out), .in2(or_1_out), .in3(nor_1_out), .in4(xor_1_out), .out(result),
    .sel(op));  // open: in5, in6, in7, en
endmodule
