// Logisim project CPU.circ as structural Verilog: 1 circuit, main circuit main
module main (
);

  wire clock_1_out, main_1_p2, main_1_p3, main_1_p4, main_1_p5, main_1_p7, main_1_p8, main_1_p9, main_1_p10;
  wire [1:0] multiplexer_1_out;
  wire [2:0] main_1_p6;
  wire [3:0] main_1_p1;
  wire [5:0] rom_1_data;
  wire [7:0] adder_1_out, register_1_q;
  wire [9:0] bit_extender_1_out, main_2_register_1_data, main_2_register_2_data, main_3_result,
       multiplexer_2_out, multiplexer_3_out, multiplexer_4_out, ram_1_data;

  // ControlUnit_main main_1: pin names not known; wires that end beside it: main_1_p1, main_1_p2, main_1_p3, main_1_p4, main_1_p5, main_1_p6, main_1_p7, main_1_p8, main_1_p9, main_1_p10
  Register register_1 (.D(adder_1_out), .Q(register_1_q), .clk(clock_1_out));  // open: en, clr
  Clock clock_1 (.out(clock_1_out));
  Adder adder_1 (.a(register_1_q), .b(8'h1), .out(adder_1_out));  // open: cin, cout
  ROM #(.dataWidth(10)) rom_1 (.addr(register_1_q), .data({main_1_p1, rom_1_data}));  // open: sel
  Multiplexer #(.width(2)) multiplexer_1 (
    .in0(rom_1_data[1:0]), .in1(rom_1_data[3:2]), .out(multiplexer_1_out), .sel(main_1_p3));  // open: en
  _10_bits__Register_File_main main_2 (
    .Data(multiplexer_4_out), .CLK(clock_1_out), .Register_1_Data(main_2_register_1_data),
    .Register_2_Data(main_2_register_2_data), .Write__Register(multiplexer_1_out),
    .Write_Register(main_1_p2), .Read_register_1(rom_1_data[5:4]), .Read_Register_2(rom_1_data[3:2]));
  assign bit_extender_1_out = {{8{1'b0}}, rom_1_data[1:0]};  // Bit_Extender bit_extender_1
  Multiplexer #(.width(10)) multiplexer_2 (
    .in0(main_2_register_2_data), .in1(bit_extender_1_out), .out(multiplexer_2_out), .sel(main_1_p4));  // open: en
  _10bit_alu_main main_3 (
    .Op(main_1_p6), .Result(main_3_result), .B(multiplexer_2_out), .A(main_2_register_1_data),
    .B_prime(main_1_p9), .Cin(main_1_p9));  // open: Cout
  RAM #(.addrWidth(10), .dataWidth(10), .bus("separate")) ram_1 (
    .addr(main_3_result), .din(main_2_register_2_data), .data(ram_1_data), .str(main_1_p8),
    .clk(clock_1_out), .ld(main_1_p7));  // open: sel, clr
  Multiplexer #(.width(10)) multiplexer_3 (
    .in0(main_3_result), .in1(ram_1_data), .out(multiplexer_3_out), .sel(main_1_p5));  // open: en
  Multiplexer #(.width(10)) multiplexer_4 (
    .in0(multiplexer_3_out), .out(multiplexer_4_out), .sel(main_1_p10));  // open: in1, en

  // Notes on the sheet:
  //   contents of rom_1 (hex, n*v repeats v):
  //   b 5e 87 cb 14b 18f 26f
endmodule
