// Logisim project 10 bits  Register File.circ as structural Verilog: 1 circuit, main circuit main
module main (
  input  [1:0] Write__Register,
  input  [1:0] Read_register_1,
  input  [9:0] Data,
  input  Write_Register,
  input  CLK,
  input  [1:0] Read_Register_2,
  output [9:0] Register_1_Data,
  output [9:0] Register_2_Data
);

  wire decoder_1_out0, decoder_1_out1, decoder_1_out2, decoder_1_out3;
  wire [9:0] multiplexer_1_out, s0_q, s1_q, t1_q, to_q;

  Decoder #(.select(2)) decoder_1 (
    .out0(decoder_1_out0), .out1(decoder_1_out1), .out2(decoder_1_out2), .out3(decoder_1_out3),
    .sel(Write__Register));  // open: en
  Multiplexer #(.width(10)) multiplexer_1 (.in1(Data), .out(multiplexer_1_out), .sel(Write_Register));  // open: in0, en
  Register #(.width(10)) to (.D(multiplexer_1_out), .en(decoder_1_out0), .Q(to_q), .clk(CLK));  // open: clr
  Register #(.width(10)) t1 (.D(multiplexer_1_out), .en(decoder_1_out1), .Q(t1_q), .clk(CLK));  // open: clr
  Register #(.width(10)) s0 (.D(multiplexer_1_out), .en(decoder_1_out2), .Q(s0_q), .clk(CLK));  // open: clr
  Register #(.width(10)) s1 (.D(multiplexer_1_out), .en(decoder_1_out3), .Q(s1_q), .clk(CLK));  // open: clr
  Multiplexer #(.select(2), .width(10)) multiplexer_2 (
    .in0(to_q), .in1(t1_q), .in2(s0_q), .in3(s1_q), .out(Register_1_Data), .sel(Read_register_1));  // open: en
  Multiplexer #(.select(2), .width(10)) multiplexer_3 (
    .in0(to_q), .in1(t1_q), .in2(s0_q), .in3(s1_q), .out(Register_2_Data), .sel(Read_Register_2));  // open: en
endmodule
